# Fritzing sketch nGeigieTeensy (saved by Fritzing 0.9.0b)
breadboards: 1

parts:
  Part1 = OpenLog
  Teensy_3_1 = Teensy 3.1
  U1 = MAX1555 Lithium Charger IC [package=sot23-5]
  LED1 = smd LED [color="Yellow (595nm)" package="0603 [SMD]"]
  LCD1 = LCD screen
  U2 = LIPO-2000mAh [package=lipo-2000]
  R1 = Resistor [tolerance=±5% resistance=220 package=THT]
  J2 = Screw terminal - 5 pins [package=THT]
  WIZ820io1 = WIZ820io [part_number=WIZ820io]

nets:
  N1: Part1.DTR, Teensy_3_1.D5
  N2: Part1.RXI, Teensy_3_1.D6
  N3: Part1.TXO, Teensy_3_1.D7
  VCC: Part1.VCC, Teensy_3_1.3V3, LCD1.VDD, J2.pin2, WIZ820io1.VIN
  GND: Teensy_3_1.GND, Teensy_3_1.AGND, U1.GND, LCD1.VSS, LCD1.LED-, U2.-, R1.Pin_1, J2.pin1, WIZ820io1.GND
  N4: Teensy_3_1.VBat, U1.DC
  N5: Teensy_3_1.VUSB, U1.USB
  N6: U1.CHG, LED1.anode
  N7: U1.BATT, U2.+
  N8: LED1.cathode, R1.Pin_0

notes:
  nGeigieTeensy , nGeigieTeensy version 0.5 draft, V0.5

custom parts:
  Screw terminal - 5 pins: Screw terminal with 5 pins
